# Fritzing sketch zamok (saved by Fritzing 0.9.2b)
breadboards: 1

parts:
  S1 = Momentary Switch [package=ksa_sealed_tac_switch]
  S2 = Momentary Switch [package=ksa_sealed_tac_switch]
  S3 = Momentary Switch [package=ksa_sealed_tac_switch]
  Part1 = Arduino Nano (Rev3.0)

nets:
  N1: S1.1, Part1.D13/SCK
  N2: S1.3, S2.3, S3.3, Part1.D10
  N3: S2.1, Part1.D12/MISO
  N4: S3.1, Part1.D11/MOSI

// code stored in the sketch: zamok.ino
void setup() {

}

void loop() {

}
